# Fritzing sketch Arduino_01 (saved by Fritzing 0.9.3b)
breadboards: 1

parts:
  Bauteil1 = Arduino Uno (Rev3)
  LED1 = LED - 5mm [color="Red (633nm)" package="5 mm [THT]"]
  LED2 = LED - 5mm [color="Red (633nm)" package="5 mm [THT]"]
  LED3 = LED - 5mm [color="Red (633nm)" package="5 mm [THT]"]
  R1 = Resistor [tolerance=±5% resistance=220 package=THT]
  R2 = Resistor [tolerance=±5% resistance=220 package=THT]
  R3 = Resistor [tolerance=±5% resistance=220 package=THT]
  S1 = Pushbutton [package="[THT]"]
  R4 = Resistor [tolerance=±5% resistance=100 package=THT]

nets:
  N1: Bauteil1.D2, S1.Pin_1, S1.Pin_2, R4.Pin_1
  N2: Bauteil1.D5_PWM, LED3.anode
  N3: Bauteil1.D6_PWM, LED2.anode
  N4: Bauteil1.D7, LED1.anode
  N5: Bauteil1.5V, S1.Pin_3, S1.Pin_4
  N6: Bauteil1.GND, R1.Pin_0, R2.Pin_0, R3.Pin_0, R4.Pin_0
