# Fritzing sketch Arduino_02 (saved by Fritzing 0.9.3b)
breadboards: 1

parts:
  Bauteil1 = Arduino Uno (Rev3)
  T1 = TMP36 Temperature Sensor [package="TO92 [THT]"]
  LED1 = LED - 5mm [color="Red (633nm)" package="5 mm [THT]"]
  LED2 = LED - 5mm [color="Red (633nm)" package="5 mm [THT]"]
  LED3 = LED - 5mm [color="Red (633nm)" package="5 mm [THT]"]
  R1 = Resistor [tolerance=±5% resistance=220 package=THT]
  R2 = Resistor [tolerance=±5% resistance=220 package=THT]
  R3 = Resistor [tolerance=±5% resistance=220 package=THT]

nets:
  N1: Bauteil1.A0, T1.Vout
  N2: Bauteil1.D5_PWM, LED2.anode
  N3: Bauteil1.D6_PWM, LED3.anode
  N4: Bauteil1.D7, LED1.anode
  N5: Bauteil1.5V, T1.+Vs
  GND: Bauteil1.GND, T1.GND, R1.Pin_0, R2.Pin_0, R3.Pin_0
  N6: LED1.cathode, R1.Pin_1
  N7: LED2.cathode, R3.Pin_1
  N8: LED3.cathode, R2.Pin_1
